# Fritzing sketch AnalogInputThermistor (saved by Fritzing 0.1.11)
breadboards: 1

parts:
  Arduino1 = Arduino Diecimila (deprecated) [package=THT]
  R1 = Temperature Sensor (Thermistor) [package=THT]
  R2 = 1k Ω Resistor [package=THT]

nets:
  N1: Arduino1.GND, R2.Pin_0
  N2: Arduino1.+5V, R1.pin_0
  N3: Arduino1.A2, R1.pin_1, R2.Pin_1
