# Fritzing sketch AnalogInputToServo (saved by Fritzing 0.1.b)
breadboards: 1

parts:
  Arduino1 = Arduino Diecimila (deprecated) [package=THT]
  R1 = Trimmer Potentiometer [package=THT]
  LED1 = Red LED - 5mm
  J1 = Basic Servo

nets:
  GND: Arduino1.GND, R1.leg2, LED1.cathode, J1.gnd
  N1: Arduino1.D13, LED1.anode
  N2: Arduino1.D2, J1.pulse
  +5V: Arduino1.+5V, R1.leg1, J1.vcc
  N3: Arduino1.A2, R1.wiper
