# Fritzing sketch Blink (saved by Fritzing 0.1.b)

parts:
  Arduino1 = Arduino Diecimila (deprecated) [package=THT]
  LED1 = Red LED - 5mm

nets:
  N1: Arduino1.GND, Arduino1.ground, LED1.cathode
  N2: Arduino1.D13, LED1.anode
