# Fritzing sketch Button (saved by Fritzing 0.1.b)
breadboards: 1

parts:
  Arduino1 = Arduino Diecimila (deprecated) [package=THT]
  LED1 = Red LED - 5mm
  S1 = Pushbutton [package=THT]
  Part1 = 10k Ω Resistor [package=THT]

nets:
  N1: Arduino1.GND, LED1.cathode, Part1.Pin_0
  N2: Arduino1.D13, LED1.anode
  N3: Arduino1.D2, S1.leg1, Part1.Pin_1
  N4: Arduino1.+5V, S1.leg0
