# Fritzing sketch Loop (saved by Fritzing 0.1.b)
breadboards: 1

parts:
  Arduino1 = Arduino Diecimila (deprecated) [package=THT]
  LED1 = Red LED - 5mm
  Part1 = 220 Ω Resistor [package=THT]
  LED2 = Red LED - 5mm
  Part2 = 220 Ω Resistor [package=THT]
  LED3 = Red LED - 5mm
  Part3 = 220 Ω Resistor [package=THT]
  LED4 = Red LED - 5mm
  Part4 = 220 Ω Resistor [package=THT]
  LED5 = Red LED - 5mm
  Part5 = 220 Ω Resistor [package=THT]
  LED6 = Red LED - 5mm
  Part6 = 220 Ω Resistor [package=THT]

nets:
  N1: Arduino1.GND, LED1.cathode, LED2.cathode, LED3.cathode, LED4.cathode, LED5.cathode, LED6.cathode
  N2: Arduino1.D7, Part1.Pin_1
  N3: Arduino1.D6, Part2.Pin_1
  N4: Arduino1.D5, Part3.Pin_1
  N5: Arduino1.D4, Part4.Pin_1
  N6: Arduino1.D3, Part5.Pin_1
  N7: Arduino1.D2, Part6.Pin_1
  N8: LED1.anode, Part1.Pin_0
  N9: LED2.anode, Part2.Pin_0
  N10: LED3.anode, Part3.Pin_0
  N11: LED4.anode, Part4.Pin_0
  N12: LED5.anode, Part5.Pin_0
  N13: LED6.anode, Part6.Pin_0
