# Fritzing sketch npnPowerTransistor (saved by Fritzing 0.1.b)
breadboards: 1

parts:
  Arduino1 = Arduino Diecimila (deprecated) [package=THT]
  Q1 = npn-Powertransistor [package="TO220 [THT]"]
  Part1 = 1k Ω Resistor [package=THT]
  Part2 = 220 Ω Resistor [package=THT]
  LED1 = Red LED - 5mm
  LED2 = Red LED - 5mm
  Part3 = 220 Ω Resistor [package=THT]
  LED3 = Red LED - 5mm
  Part4 = 220 Ω Resistor [package=THT]
  LED4 = Red LED - 5mm
  Part5 = 220 Ω Resistor [package=THT]

nets:
  N1: Arduino1.GND, Q1.emitter
  N2: Arduino1.D9, Part1.Pin_0
  N3: Arduino1.+5V, Part2.Pin_1, Part3.Pin_1, Part4.Pin_1, Part5.Pin_1
  N4: Q1.base, Part1.Pin_1
  N5: Q1.collector, LED1.cathode, LED2.cathode, LED3.cathode, LED4.cathode
  N6: Part2.Pin_0, LED1.anode
  N7: LED2.anode, Part3.Pin_0
  N8: LED3.anode, Part4.Pin_0
  N9: LED4.anode, Part5.Pin_0
