# Fritzing sketch VoltageRegulator_with_switch (saved by Fritzing 0.11.b)
breadboards: 1

parts:
  S1 = Toggle Switch [package=THT]
  C1 = Electrolytic Capacitor [package=THT]
  C2 = Electrolytic Capacitor [package=THT]
  U1 = Voltage Regulator - 5V [package="TO220 [THT]"]

nets:
  N1: S1.L2, C1.+, U1.input_voltage
  N2: C1.-, C2.-, U1.GND
  N3: C2.+, U1.output_voltage
