# Fritzing sketch AnalogInputOutput (saved by Fritzing 0.3.15b)
breadboards: 1

parts:
  R3 = Rotary Potentiometer (Large) [package=THT]
  Arduino2 = Arduino
  R4 = Resistor [resistance=220 package=THT]
  LED2 = Red LED - 5mm

nets:
  N1: R3.leg1, Arduino2.+5V
  N2: R3.wiper, Arduino2.A3
  N3: R3.leg2, Arduino2.GND, LED2.cathode
  N4: Arduino2.D3, R4.Pin_1
  N5: R4.Pin_0, LED2.anode

notes:
  In this example, potentiometer values are read in through an 'Analog In' pin. The values are then used to control the modulation of an LED on a PWM pin. Related examples: http://arduino.cc/en/Tutorial/AnalogInput http://arduino.cc/en/Tutorial/Fading
