# Fritzing sketch AnalogInputThermistor (saved by Fritzing 0.3.9b)
breadboards: 1

parts:
  R1 = Temperature Sensor (Thermistor) [package=THT]
  LED1 = Blue LED - 5mm
  Arduino2 = Arduino
  R3 = Resistor [resistance=1k package=THT]

nets:
  N1: R1.pin_0, Arduino2.+5V
  N2: R1.pin_1, Arduino2.A2, R3.Pin_1
  N3: LED1.cathode, Arduino2.GND, R3.Pin_0
  N4: LED1.anode, Arduino2.D13

notes:
  In this example, thermistor values are read in through an 'Analog In' pin. The values are then used to control the blinking rate of an LED. Using a multimeter, check the min and max resistance of the thermistor in different light conditions. Then calculate the resistor's value with the Axel-Benz formula:
  Rref = sqrt(Rmin*Rmax)
  Related example: http://arduino.cc/en/Tutorial/AnalogInput
