# Fritzing sketch ArduinoISP (saved by Fritzing 0.7.0b)
breadboards: 1

parts:
  R1 = Resistor [resistance=1k tolerance=±5% package=THT]
  ATMEGA = atmega168 [package="DIP28 [THT]"]
  RESET = Pushbutton [package="[THT]"]
  R2 = Resistor [resistance=220 tolerance=±5% package=THT]
  R3 = Resistor [resistance=220 tolerance=±5% package=THT]
  R4 = Resistor [resistance=220 tolerance=±5% package=THT]
  R5 = Resistor [resistance=220 tolerance=±5% package=THT]
  ERROR = LED - 5mm [color="Red (633nm)" package="5 mm [THT]"]
  OSC = Resonator [frequency="16 Mhz" package=THT]
  HELLO = LED - 5mm [color="Green (555nm)" package="5 mm [THT]"]
  PULSE = LED - 5mm [color="Green (555nm)" package="5 mm [THT]"]
  PROG = LED - 5mm [color="Yellow (585nm)" package="5 mm [THT]"]
  Arduino_ISP = Arduino

nets:
  5V: R1.Pin_0, ATMEGA.Pin_7, ATMEGA.Pin_20, Arduino_ISP.+5V
  N1: R1.Pin_1, ATMEGA.Pin_1, RESET.Pin_1, RESET.Pin_2, Arduino_ISP.D10
  GND: ATMEGA.Pin_8, ATMEGA.Pin_22, RESET.Pin_3, RESET.Pin_4, R2.Pin_0, R3.Pin_1, R4.Pin_1, R5.Pin_1, OSC.GND, Arduino_ISP.GND
  N2: ATMEGA.Pin_9, OSC.0
  N3: ATMEGA.Pin_10, OSC.pin_1
  N4: ATMEGA.Pin_14, HELLO.anode
  N5: ATMEGA.Pin_17, Arduino_ISP.D11
  N6: ATMEGA.Pin_18, Arduino_ISP.D12
  N7: ATMEGA.Pin_19, Arduino_ISP.D13
  N8: R2.Pin_1, HELLO.cathode
  N9: R3.Pin_0, PULSE.cathode
  N10: R4.Pin_0, ERROR.cathode
  N11: R5.Pin_0, PROG.cathode
  N12: ERROR.anode, Arduino_ISP.D8
  N13: PULSE.anode, Arduino_ISP.D9
  N14: PROG.anode, Arduino_ISP.D7

notes:
  Using an Arduino as ISP:
  http://arduino.cc/en/Tutorial/ArduinoISP

// code stored in the sketch: ___lockfile___.txt

