# Fritzing sketch Button-SMD (saved by Fritzing 0.7.0b)
breadboards: 1

parts:
  S1 = Pushbutton [package=THT]
  Arduino2 = Arduino
  R1 = Resistor [tolerance=±5% resistance=10k package="0805 [SMD]"]
  LED1 = smd LED [color="Red (633nm)" package="0805 [SMD]"]

nets:
  N1: S1.leg0, Arduino2.+5V
  N2: S1.leg1, Arduino2.D2, R1.Pin_1
  N3: Arduino2.GND, R1.Pin_0, LED1.cathode
  N4: Arduino2.D13, LED1.anode

notes:
  In this example, a pushbutton is used as a digital input and an LED is a digital output. Related example: http://arduino.cc/en/Tutorial/Button

// code stored in the sketch: ___lockfile___.txt

