# Fritzing sketch Button (saved by Fritzing 0.3.9b)
breadboards: 1

parts:
  LED1 = Red LED - 5mm
  S1 = Pushbutton [package=THT]
  Arduino2 = Arduino
  R2 = Resistor [resistance=10k package=THT]

nets:
  N1: LED1.cathode, Arduino2.GND, R2.Pin_0
  N2: LED1.anode, Arduino2.D13
  N3: S1.leg0, Arduino2.+5V
  N4: S1.leg1, Arduino2.D2, R2.Pin_1

notes:
  In this example, a pushbutton is used as a digital input and an LED is a digital output. Related example: http://arduino.cc/en/Tutorial/Button
