# Fritzing sketch CosmicRayGun (saved by Fritzing 0.7.0b)
breadboards: 1

parts:
  Arduino = Arduino
  R6 = Resistor [resistance=220 tolerance=±5% package=THT]
  R5 = Resistor [resistance=220 tolerance=±5% package=THT]
  R4 = Resistor [resistance=220 tolerance=±5% package=THT]
  R3 = Resistor [resistance=220 tolerance=±5% package=THT]
  R2 = Resistor [resistance=220 tolerance=±5% package=THT]
  R1 = Resistor [resistance=220 tolerance=±5% package=THT]
  S2 = Pushbutton [package=THT]
  R7 = Resistor [resistance=1k tolerance=±5% package=THT]
  R8 = Resistor [resistance=1k tolerance=±5% package=THT]
  S1 = Pushbutton [package=THT]
  Speaker = Piezo Speaker
  LED5 = LED - 5mm [color="Red (633nm)" package="5 mm [THT]"]
  LED6 = LED - 5mm [color="Red (633nm)" package="5 mm [THT]"]
  LED3 = LED - 5mm [color="Yellow (585nm)" package="5 mm [THT]"]
  LED1 = LED - 5mm [color="Green (555nm)" package="5 mm [THT]"]
  LED4 = LED - 5mm [color="Yellow (585nm)" package="5 mm [THT]"]
  LED2 = LED - 5mm [color="Green (555nm)" package="5 mm [THT]"]

nets:
  N1: Arduino.GND, R7.Pin_0, R8.Pin_0, LED5.cathode, LED6.cathode, LED3.cathode, LED1.cathode, LED4.cathode, LED2.cathode
  N2: Arduino.D13, R8.Pin_1, S1.leg0
  N3: Arduino.D12, R1.Pin_0
  N4: Arduino.D11, R2.Pin_0
  N5: Arduino.D10, R3.Pin_0
  N6: Arduino.D9, R4.Pin_0
  N7: Arduino.D8, R5.Pin_0
  N8: Arduino.D7, R6.Pin_0
  N9: Arduino.D5, S2.leg1, R7.Pin_1
  N10: Arduino.D3, Speaker.pin2
  N11: Arduino.D2, Speaker.pin1
  N12: Arduino.+5V, S2.leg0, S1.leg1
  N13: R6.Pin_1, LED1.anode
  N14: R5.Pin_1, LED2.anode
  N15: R4.Pin_1, LED3.anode
  N16: R3.Pin_1, LED4.anode
  N17: R2.Pin_1, LED5.anode
  N18: R1.Pin_1, LED6.anode

notes:
  Get the code from the Fritzing Project Page:
  Cosmic Raygun

// code stored in the sketch: ___lockfile___.txt

