# Fritzing sketch Curvy-Parking-Assistant (saved by Fritzing 0.7.0b)
breadboards: 1

parts:
  IR_Sensor_1 = Infrared Proximity Sensor
  IR_Sensor_2 = Infrared Proximity Sensor
  220Ω = Resistor [resistance=220 tolerance=±5% package=THT]
  220Ω_2 = Resistor [resistance=220 tolerance=±5% package=THT]
  220Ω_3 = Resistor [resistance=220 tolerance=±5% package=THT]
  220Ω_4 = Resistor [resistance=220 tolerance=±5% package=THT]
  220Ω_5 = Resistor [resistance=220 tolerance=±5% package=THT]
  220Ω_6 = Resistor [resistance=220 tolerance=±5% package=THT]
  220Ω_7 = Resistor [resistance=220 tolerance=±5% package=THT]
  220Ω_8 = Resistor [resistance=220 tolerance=±5% package=THT]
  220Ω_9 = Resistor [resistance=220 tolerance=±5% package=THT]
  220Ω_10 = Resistor [resistance=220 tolerance=±5% package=THT]
  LED5 = LED - 5mm [color="Red (633nm)" package="5 mm [THT]"]
  LED6 = LED - 5mm [color="Red (633nm)" package="5 mm [THT]"]
  LED2 = LED - 5mm [color="Yellow (585nm)" package="5 mm [THT]"]
  LED4 = LED - 5mm [color="Red (633nm)" package="5 mm [THT]"]
  LED3 = LED - 5mm [color="Red (633nm)" package="5 mm [THT]"]
  LED2_2 = LED - 5mm [color="Yellow (585nm)" package="5 mm [THT]"]
  LED2_3 = LED - 5mm [color="Yellow (585nm)" package="5 mm [THT]"]
  LED2_4 = LED - 5mm [color="Yellow (585nm)" package="5 mm [THT]"]
  LED2_5 = LED - 5mm [color="Yellow (585nm)" package="5 mm [THT]"]
  LED2_6 = LED - 5mm [color="Yellow (585nm)" package="5 mm [THT]"]
  Parking_Assistant = Arduino

nets:
  N1: IR_Sensor_1.Vout, Parking_Assistant.A1
  GND: IR_Sensor_1.GND, IR_Sensor_2.GND, LED5.cathode, LED6.cathode, LED2.cathode, LED4.cathode, LED3.cathode, LED2_2.cathode, LED2_3.cathode, LED2_4.cathode, LED2_5.cathode, LED2_6.cathode, Parking_Assistant.GND
  5V: IR_Sensor_1.Vcc, IR_Sensor_2.Vcc, Parking_Assistant.+5V
  N2: IR_Sensor_2.Vout, Parking_Assistant.A0
  N3: 220Ω.Pin_0, LED6.anode
  N4: 220Ω.Pin_1, Parking_Assistant.D12
  N5: 220Ω_2.Pin_0, LED5.anode
  N6: 220Ω_2.Pin_1, Parking_Assistant.D11
  N7: 220Ω_3.Pin_0, LED2_2.anode
  N8: 220Ω_3.Pin_1, Parking_Assistant.D10
  N9: 220Ω_4.Pin_0, LED2_6.anode
  N10: 220Ω_4.Pin_1, Parking_Assistant.D8
  N11: 220Ω_5.Pin_0, LED2_5.anode
  N12: 220Ω_5.Pin_1, Parking_Assistant.D9
  N13: 220Ω_6.Pin_0, LED2_3.anode
  N14: 220Ω_6.Pin_1, Parking_Assistant.D6
  N15: 220Ω_7.Pin_0, LED2_4.anode
  N16: 220Ω_7.Pin_1, Parking_Assistant.D5
  N17: 220Ω_8.Pin_0, LED3.anode
  N18: 220Ω_8.Pin_1, Parking_Assistant.D3
  N19: 220Ω_9.Pin_0, LED4.anode
  N20: 220Ω_9.Pin_1, Parking_Assistant.D2
  N21: 220Ω_10.Pin_0, LED2.anode
  N22: 220Ω_10.Pin_1, Parking_Assistant.D4

notes:
  Simple Parking Assistant
  The distance to objects in the proximity is measured and displayed as led graph.

// code stored in the sketch: ___lockfile___.txt

