# Fritzing sketch EDGY-motor-control (saved by Fritzing 0.7.0b)
breadboards: 1

parts:
  EDGY_motor_control1 = EDGY
  M1 = DC Motor
  Arduino1 = Arduino

nets:
  VIN: EDGY_motor_control1.Vin, EDGY_motor_control1.5V+, Arduino1.+5V
  N1: EDGY_motor_control1.A2, Arduino1.D5
  N2: EDGY_motor_control1.B2, Arduino1.D4
  N3: EDGY_motor_control1.Speed2, Arduino1.D3
  GND: EDGY_motor_control1.GND, Arduino1.GND
  N4: EDGY_motor_control1.B2out, M1.pin_2
  N5: EDGY_motor_control1.A2out, M1.pin_1

// code stored in the sketch: ___lockfile___.txt

