# Fritzing sketch Loop (saved by Fritzing 0.3.15b)
breadboards: 1

parts:
  Arduino = Arduino
  R7 = Resistor [resistance=220 package=THT]
  R8 = Resistor [resistance=220 package=THT]
  R9 = Resistor [resistance=220 package=THT]
  R10 = Resistor [resistance=220 package=THT]
  R11 = Resistor [resistance=220 package=THT]
  R12 = Resistor [resistance=220 package=THT]
  LED7 = Red LED - 5mm
  LED8 = Red LED - 5mm
  LED9 = Red LED - 5mm
  LED10 = Red LED - 5mm
  LED11 = Red LED - 5mm
  LED12 = Red LED - 5mm

nets:
  N1: Arduino.GND, LED7.cathode, LED8.cathode, LED9.cathode, LED10.cathode, LED11.cathode, LED12.cathode
  N2: Arduino.D7, R12.Pin_1
  N3: Arduino.D6, R11.Pin_1
  N4: Arduino.D5, R7.Pin_1
  N5: Arduino.D4, R8.Pin_1
  N6: Arduino.D3, R10.Pin_1
  N7: Arduino.D2, R9.Pin_1
  N8: R7.Pin_0, LED9.anode
  N9: R8.Pin_0, LED10.anode
  N10: R9.Pin_0, LED11.anode
  N11: R10.Pin_0, LED7.anode
  N12: R11.Pin_0, LED8.anode
  N13: R12.Pin_0, LED12.anode

notes:
  In this example, six leds are controlled by digital out pins. Related Example: http://arduino.cc/en/Tutorial/Loop
