# Fritzing sketch Optocoupler (saved by Fritzing 0.2.2)
breadboards: 1

parts:
  U1 = Optocoupler [package=THT]
  Arduino1 = Arduino Diecimila (deprecated) [package=THT]
  VCC1 = obsolete Battery
  LED1 = Red LED - 5mm
  R1 = 220 Ω Resistor [package=THT]
  R2 = 220 Ω Resistor [package=THT]

nets:
  N1: U1.Pin_1, R2.Pin_1
  N2: U1.Pin_2, Arduino1.GND
  N3: U1.Pin_4, VCC1.-
  N4: U1.Pin_5, LED1.cathode
  N5: Arduino1.D11, R2.Pin_0
  N6: VCC1.+, R1.Pin_1
  N7: LED1.anode, R1.Pin_0

notes:
  An optocoupler can be used to control a circuit that's completely isolated from your microcontroller. In this case, imagine that the LED and battery pack are a hacked toy which you're turning on and off with Arduino.
