# Fritzing sketch Relay (saved by Fritzing 0.3.9b)
breadboards: 1

parts:
  K1 = Relay [package=THT]
  Arduino1 = Arduino
  Q1 = NPN-Transistor [package="TO92 [THT]"]
  D1 = Rectifier Diode [package=THT]
  Power_plug1 = Power plug
  M1 = DC Motor
  R3 = Resistor [resistance=1k package=THT]

nets:
  N1: K1.A, M1.pin_1
  N2: K1.COIL1, Q1.collector, D1.anode
  N3: K1.C1, K1.C2, Power_plug1.VCC
  N4: K1.COIL2, Arduino1.+5V, D1.cathode
  N5: Arduino1.D3, R3.Pin_1
  N6: Arduino1.GND, Q1.emitter
  N7: Q1.base, R3.Pin_0
  N8: Power_plug1.GND, M1.pin_2

notes:
  In this circuit a 5V relay is connected to the arduino board and controls a DC motor which is connected to an external power supply.
