# Fritzing sketch Shift_Register (saved by Fritzing 0.3.9b)
breadboards: 2

parts:
  74HC5951 = 74HC595 [package="DIP16 [THT]"]
  Arduino1 = Arduino
  C1 = Ceramic Capacitor [package=THT]
  LED1 = Red LED - 5mm
  LED1_2 = Red LED - 5mm
  LED1_3 = Red LED - 5mm
  LED1_4 = Red LED - 5mm
  LED1_5 = Red LED - 5mm
  LED1_6 = Red LED - 5mm
  LED1_7 = Red LED - 5mm
  LED1_8 = Red LED - 5mm
  R2 = Resistor [resistance=220 package=THT]
  R3 = Resistor [resistance=220 package=THT]
  R4 = Resistor [resistance=220 package=THT]
  R5 = Resistor [resistance=220 package=THT]
  R6 = Resistor [resistance=220 package=THT]
  R7 = Resistor [resistance=220 package=THT]
  R8 = Resistor [resistance=220 package=THT]
  R9 = Resistor [resistance=220 package=THT]

nets:
  N1: 74HC5951.Q1, R5.Pin_1
  N2: 74HC5951.Q2, R6.Pin_1
  N3: 74HC5951.Q3, R7.Pin_1
  N4: 74HC5951.Q4, R9.Pin_1
  N5: 74HC5951.Q5, R2.Pin_1
  N6: 74HC5951.Q6, R3.Pin_1
  N7: 74HC5951.Q7, R8.Pin_1
  GND: 74HC5951.GND, 74HC5951.OE, Arduino1.GND, C1.pin_1, LED1.cathode, LED1_2.cathode, LED1_3.cathode, LED1_4.cathode, LED1_5.cathode, LED1_6.cathode, LED1_7.cathode, LED1_8.cathode
  VCC: 74HC5951.MR, 74HC5951.VCC, Arduino1.+5V
  N8: 74HC5951.SH_CP, Arduino1.D12
  N9: 74HC5951.ST_CP, Arduino1.D8, C1.pin_0
  N10: 74HC5951.DS, Arduino1.D11
  N11: 74HC5951.Q0, R4.Pin_1
  N12: LED1.anode, R4.Pin_0
  N13: LED1_2.anode, R5.Pin_0
  N14: LED1_3.anode, R6.Pin_0
  N15: LED1_4.anode, R3.Pin_0
  N16: LED1_5.anode, R7.Pin_0
  N17: LED1_6.anode, R9.Pin_0
  N18: LED1_7.anode, R8.Pin_0
  N19: LED1_8.anode, R2.Pin_0

notes:
  In this project, a 74HC595 shift register is used to control 8 LEDs with just 3 Arduino pins.
  Related example: http://www.arduino.cc/en/Tutorial/ShiftOut
