# Fritzing sketch Stepper_Motor (saved by Fritzing 0.3.9b)
breadboards: 1

parts:
  Arduino1 = Arduino
  IC1 = H-Bridge [package=THT]
  M1 = Stepper Motor - Bipolar
  Q1 = NPN-Transistor [package="TO92 [THT]"]
  Power_plug1 = Power plug
  Q2 = NPN-Transistor [package="TO92 [THT]"]
  R10 = Resistor [resistance=1k package=THT]
  R11 = Resistor [resistance=10k package=THT]
  R12 = Resistor [resistance=10k package=THT]
  R13 = Resistor [resistance=1k package=THT]

nets:
  GND: Arduino1.GND, IC1.GND1, IC1.GND2, IC1.GND3, IC1.GND4, Q1.emitter, Power_plug1.GND, Q2.emitter
  N1: Arduino1.D11, IC1.4A, R12.Pin_1, R13.Pin_1
  N2: Arduino1.D10, IC1.1A, R10.Pin_1
  N3: Arduino1.+5V, IC1.1_2EN, IC1.3_4EN, IC1.VCC1, R11.Pin_0
  N4: IC1.1Y, M1.A
  N5: IC1.2Y, M1.C
  N6: IC1.2A, Q1.collector, R11.Pin_1
  N7: IC1.VCC2, Power_plug1.VCC
  N8: IC1.3A, Q2.collector, R12.Pin_0
  N9: IC1.3Y, M1.D
  N10: IC1.4Y, M1.B
  N11: Q1.base, R10.Pin_0
  N12: Q2.base, R13.Pin_0

notes:
  This project shows how to control a stepper motor's direction (running forwards and backwards) using an H-bridge. An H-bridge is an electronic circuit which enables a voltage to be applied across a load in either direction.
  Related Examples: Stepper Motor Control
