# Fritzing sketch TrafficLight (saved by Fritzing 0.3.15b)
breadboards: 1

parts:
  Arduino2 = Arduino
  LED6 = green LED - 5mm
  R7 = Resistor [resistance=220 package=THT]
  S2 = Pushbutton [package=THT]
  LED7 = yellow LED - 5mm
  R8 = Resistor [resistance=220 package=THT]
  LED8 = green LED - 5mm
  R9 = Resistor [resistance=220 package=THT]
  LED9 = Red LED - 5mm
  R10 = Resistor [resistance=220 package=THT]
  LED10 = Red LED - 5mm
  R11 = Resistor [resistance=220 package=THT]
  R12 = Resistor [resistance=220 package=THT]

nets:
  N1: Arduino2.GND, LED6.cathode, LED7.cathode, LED8.cathode, LED9.cathode, LED10.cathode, R11.Pin_0
  N2: Arduino2.D12, R7.Pin_1
  N3: Arduino2.D11, R9.Pin_1
  N4: Arduino2.D10, R10.Pin_1
  N5: Arduino2.D9, R8.Pin_1
  N6: Arduino2.D8, R12.Pin_1
  N7: Arduino2.D2, S2.leg1, R11.Pin_1
  N8: Arduino2.+5V, S2.leg0
  N9: LED6.anode, R8.Pin_0
  N10: R7.Pin_0, LED10.anode
  N11: LED7.anode, R9.Pin_0
  N12: LED8.anode, R10.Pin_0
  N13: LED9.anode, R12.Pin_0

notes:
  This circuit can be coded such that both the car and pedestrian traffic lights go through their normal cycle until the button is pressed by a pedestrian. In this case, the lights will change in favor of the pedestrian.
  Car Traffic Light
  Pedestrian Traffic Light
