# Fritzing sketch VoltageRegulator_7800series (saved by Fritzing 0.3.7b)
breadboards: 1

parts:
  C1 = Electrolytic Capacitor [package=THT]
  C2 = Electrolytic Capacitor [package=THT]
  U1 = Voltage Regulator - 5V [package="TO220 [THT]"]
  Power_plug1 = Power plug
  J2 = Generic male header - 2 pins [package=THT]

nets:
  GND: C1.-, C2.-, U1.GND, Power_plug1.GND, J2.pin2
  N1: C1.+, U1.input_voltage, Power_plug1.VCC
  N2: C2.+, U1.output_voltage, J2.pin1

notes:
  This example uses a 7805 voltage regulator to regulate voltage to 5 volts. The input should be at least 7V DC.
