# Fritzing sketch color-fader (saved by Fritzing 0.7.0b)
breadboards: 1

parts:
  Arduino1 = Arduino
  LED1 = RGB LED (com. cathode, rbg) [package="5 mm [THT]"]
  R1 = Resistor [tolerance=±5% resistance=220 package=THT]
  R3 = Resistor [tolerance=±5% resistance=220 package=THT]
  R2 = Resistor [tolerance=±5% resistance=220 package=THT]
  R4 = Rotary Potentiometer (Small) [maximum_resistance=100kΩ]

nets:
  N1: Arduino1.GND, LED1.common_cathode, R4.leg1
  N2: Arduino1.D11, R1.Pin_0
  N3: Arduino1.D10, R3.Pin_0
  N4: Arduino1.D9, R2.Pin_0
  N5: Arduino1.+5V, R4.leg2
  N6: Arduino1.A0, R4.wiper
  N7: LED1.red_anode, R1.Pin_1
  N8: LED1.blue_anode, R3.Pin_1
  N9: LED1.green_anode, R2.Pin_1

notes:
  A potentiometer is used to display rainbow colors on an rgb LED. It is the type in the Fritzing Starter Kits (pins: red, com. cathode, blue, green).
  Get the Arduino-Code from here:
  http://fritzing.org/projects/color-fader/

// code stored in the sketch: ___lockfile___.txt

