# Fritzing sketch npnPowerTransistor (saved by Fritzing 0.3.15b)
breadboards: 1

parts:
  Q1 = npn-Powertransistor [package="TO220 [THT]"]
  Arduino2 = Arduino
  R6 = Resistor [resistance=220 package=THT]
  R7 = Resistor [resistance=220 package=THT]
  R8 = Resistor [resistance=1k package=THT]
  R9 = Resistor [resistance=220 package=THT]
  R10 = Resistor [resistance=220 package=THT]
  LED5 = Red LED - 5mm
  LED6 = Red LED - 5mm
  LED7 = Red LED - 5mm
  LED8 = Red LED - 5mm

nets:
  N1: Q1.base, R8.Pin_1
  N2: Q1.collector, LED5.cathode, LED6.cathode, LED7.cathode, LED8.cathode
  N3: Q1.emitter, Arduino2.GND
  N4: Arduino2.D9, R8.Pin_0
  N5: Arduino2.+5V, R6.Pin_1, R7.Pin_1, R9.Pin_1, R10.Pin_1
  N6: R6.Pin_0, LED7.anode
  N7: R7.Pin_0, LED5.anode
  N8: R9.Pin_0, LED8.anode
  N9: R10.Pin_0, LED6.anode

notes:
  Using a power transistor with an Arduino will allow you to control outputs that need more current or higher voltages than the Arduino can provide. Related example: http://itp.nyu.edu/physcomp/Tutorials/HighCurrentLoads
