# Fritzing sketch treeduino (saved by Fritzing 0.3.4b)
breadboards: 1

parts:
  PCB1 = Artreeno [package=THT]
  LED1 = Red LED - 5mm
  R1 = 220 Ω Resistor [package=THT]
  LED2 = white LED - 5mm
  R2 = 220 Ω Resistor [package=THT]
  LED5 = white LED - 5mm
  R4 = 220 Ω Resistor [package=THT]
  R6 = 220 Ω Resistor [package=THT]
  R5 = 220 Ω Resistor [package=THT]
  LED6 = Red LED - 5mm
  LED3 = white LED - 5mm
  LED4 = Red LED - 5mm
  R3 = 220 Ω Resistor [package=THT]

nets:
  GND1: PCB1.GND1, PCB1.GND2, PCB1.GND3, LED1.cathode, LED2.cathode, LED5.cathode, LED6.cathode, LED3.cathode, LED4.cathode
  N1: PCB1.digital6, R2.Pin_1
  N2: PCB1.digital5, R3.Pin_0
  N3: PCB1.digital4, R5.Pin_0
  N4: PCB1.digital3, R6.Pin_1
  N5: PCB1.digital2, R1.Pin_1
  N6: PCB1.digital1, R4.Pin_1
  N7: LED1.anode, R1.Pin_0
  N8: LED2.anode, R2.Pin_0
  N9: LED5.anode, R4.Pin_0
  N10: R6.Pin_0, LED6.anode
  N11: R5.Pin_1, LED3.anode
  N12: LED4.anode, R3.Pin_1
